# Fritzing sketch i2x-repartition-board (saved by Fritzing 0.9.6b)
breadboards: 1

parts:
  Mod1 = Raspberry Pi 4B
  Part1 = Adafruit TCA9548A
  J6 = female pin header, 2 pins [form="♀ (female)"]
  J7 = female pin header, 2 pins [form="♀ (female)"]
  J3 = female pin header, 4 pins [form="♀ (female)"]
  J9 = female alternating pin header, 4 pins [form="♀ (female)"]
  J10 = female alternating pin header, 4 pins [form="♀ (female)"]
  J11 = female alternating pin header, 4 pins [form="♀ (female)"]
  J13 = female alternating pin header, 2 pins [form="♀ (female)"]
  J17 = female alternating pin header, 2 pins [form="♀ (female)"]
  J18 = female alternating pin header, 2 pins [form="♀ (female)"]
  J19 = female alternating pin header, 2 pins [form="♀ (female)"]
  J20 = female alternating pin header, 2 pins [form="♀ (female)"]
  J21 = female alternating pin header, 2 pins [form="♀ (female)"]
  J30 = female pin header, 4 pins [form="♀ (female)"]
  J31 = female alternating pin header, 4 pins [form="♀ (female)"]
  J32 = female alternating pin header, 4 pins [form="♀ (female)"]
  J33 = female alternating pin header, 4 pins [form="♀ (female)"]
  J46 = female alternating pin header, 2 pins [form="♀ (female)"]
  J47 = female alternating pin header, 2 pins [form="♀ (female)"]
  J48 = female alternating pin header, 2 pins [form="♀ (female)"]
  J49 = female alternating pin header, 2 pins [form="♀ (female)"]
  J50 = female alternating pin header, 2 pins [form="♀ (female)"]
  J51 = female alternating pin header, 2 pins [form="♀ (female)"]
  J52 = female alternating pin header, 2 pins [form="♀ (female)"]
  J53 = female alternating pin header, 2 pins [form="♀ (female)"]

nets:
  5V: Mod1.5V, Part1.VCC, J3.pin3, J9.pin3, J10.pin3, J11.pin3, J30.pin3, J31.pin3, J32.pin3, J33.pin3, J46.pin1, J47.pin1, J48.pin1, J49.pin1, J50.pin1, J51.pin1, J52.pin1, J53.pin1
  N1: Mod1.GPIO2, Part1.INPUTSDA, J3.pin1, J9.pin1, J10.pin1, J11.pin1, J30.pin1, J31.pin1, J32.pin1, J33.pin1
  N2: Mod1.GPIO3, Part1.INPUTSCL, J3.pin2, J9.pin2, J10.pin2, J11.pin2, J30.pin2, J31.pin2, J32.pin2, J33.pin2
  GND: Mod1.GND, Part1.GND, J3.pin4, J9.pin4, J10.pin4, J11.pin4, J30.pin4, J31.pin4, J32.pin4, J33.pin4, J46.pin2, J47.pin2, J48.pin2, J49.pin2, J50.pin2, J51.pin2, J52.pin2, J53.pin2
  N3: Part1.2SDA, J13.pin2
  N4: Part1.2SCL, J13.pin1
  N5: Part1.3SDA, J17.pin2
  N6: Part1.3SCL, J17.pin1
  N7: Part1.4SDA, J18.pin2
  N8: Part1.4SCL, J18.pin1
  N9: Part1.5SDA, J6.pin2
  N10: Part1.5SCL, J6.pin1
  N11: Part1.6SDA, J20.pin2
  N12: Part1.6SCL, J20.pin1
  N13: Part1.7SDA, J19.pin2
  N14: Part1.7SCL, J19.pin1
  N15: Part1.0SDA, J21.pin1
  N16: Part1.0SCL, J21.pin2
  N17: Part1.1SDA, J7.pin1
  N18: Part1.1SCL, J7.pin2

custom parts:
  Adafruit TCA9548A: You just found the perfect I2C sensor, and you want to wire up two or three or more of them to your Arduino when you realize "Uh oh, this chip has a fixed I2C address, and from what I know about I2C, you cannot have two devices with the same address on the same SDA/SCL pins!" Are you out of luck? You would be, if you didn't have this ultra-cool TCA9548A 1-to-8 I2C multiplexer! Finally, a way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
